# Fritzing sketch pie-homecage (saved by Fritzing 0.9.3b)

parts:
  Raspberry_Pi_1 = Raspberry Pi 3 [part_number=RPI-3-V1.2]
  12V_Power = Power plug
  2-Channel_Relay = 2-Channel 5v Relay Shield [package=relay-2ch5v10a]
  LED_1 = LED - 5mm [color="White (8000K)" package="5 mm [THT]"]
  Temperature_Sensor = TRANSISTOR_NPN [package=to-92-ammo]
  LED_2 = LED - 5mm [color="Infrared (880nm)" package="5 mm [THT]"]

nets:
  N1: Raspberry_Pi_1.GPIO4, Temperature_Sensor.B
  N2: Raspberry_Pi_1.GPIO19, 2-Channel_Relay.IN1
  GND: Raspberry_Pi_1.GND, 2-Channel_Relay.GND, Temperature_Sensor.C
  N3: Raspberry_Pi_1.GPIO18, 2-Channel_Relay.IN2
  5V: Raspberry_Pi_1.5V, 2-Channel_Relay.VCC, Temperature_Sensor.E
  N4: 12V_Power.VCC, 2-Channel_Relay.K1-In, 2-Channel_Relay.K2-In
  N5: 2-Channel_Relay.K1-Off, LED_1.anode
  N6: 2-Channel_Relay.K2-Off, LED_2.anode

custom parts:
  2-Channel 5v Relay Shield: 2 Channel 5v Relay Shield w. 2x SPD-06VDC-SD-C
