# Fritzing sketch pie (saved by Fritzing 0.9.3b)
breadboards: 1

parts:
  Motor_Controller = EasyDriver_v44
  Stepper_Motor_1 = Stepper Motor - Bipolar
  Raspberry_Pi_1 = Raspberry Pi 3 [part_number=RPI-3-V1.2]
  12V_Power = Power plug
  2-Channel_Relay = 2-Channel 5v Relay Shield [package=relay-2ch5v10a]
  LED_2 = LED - 5mm [color="Infrared (880nm)" package="5 mm [THT]"]
  LED_1 = LED - 5mm [color="White (8000K)" package="5 mm [THT]"]
  Scope_Frame_Out = BNC socket [package=bnc]
  Scope_Trigger_In = BNC socket [package=bnc]
  Teensy_3_2 = Teensy 3.0 [part_number="Freescale ARM MK20DX128"]
  Scope_Trigger_Out = BNC socket [package=bnc]
  Temperature_Sensor = TRANSISTOR_NPN [package=to-92-ammo]

nets:
  GND: Motor_Controller.GND, Raspberry_Pi_1.GND, 12V_Power.GND, 2-Channel_Relay.GND, Scope_Frame_Out.GND, Scope_Trigger_In.GND, Teensy_3_2.GND, Scope_Trigger_Out.GND, Temperature_Sensor.C
  N1: Motor_Controller.V+, 12V_Power.VCC, 2-Channel_Relay.K1-In, 2-Channel_Relay.K2-In
  N2: Motor_Controller.STEP, Teensy_3_2.17
  N3: Motor_Controller.DIR, Teensy_3_2.16
  N4: Motor_Controller.OUT2A, Stepper_Motor_1.A
  N5: Motor_Controller.OUT2B, Stepper_Motor_1.C
  N6: Motor_Controller.OUT1A, Stepper_Motor_1.B
  N7: Motor_Controller.OUT1B, Stepper_Motor_1.D
  VCC: Motor_Controller.VCC, Raspberry_Pi_1.5V, 2-Channel_Relay.VCC, Temperature_Sensor.E
  N8: Motor_Controller.ENABLE, Teensy_3_2.20
  N9: Motor_Controller.RESET, Teensy_3_2.19
  N10: Raspberry_Pi_1.GPIO4, Temperature_Sensor.B
  N11: Raspberry_Pi_1.GPIO19, 2-Channel_Relay.IN1
  N12: Raspberry_Pi_1.GPIO7, Teensy_3_2.12, Teensy_3_2.VBat
  N13: Raspberry_Pi_1.GPIO8, Teensy_3_2.11
  N14: Raspberry_Pi_1.GPIO24, Teensy_3_2.9
  N15: Raspberry_Pi_1.GPIO23, Teensy_3_2.6
  N16: Raspberry_Pi_1.GPIO18, 2-Channel_Relay.IN2
  N17: Raspberry_Pi_1.GPIO15, Scope_Trigger_In.OUT, Teensy_3_2.3
  N18: 2-Channel_Relay.K1-Off, LED_1.anode
  N19: 2-Channel_Relay.K1-On, LED_1.cathode
  N20: 2-Channel_Relay.K2-Off, LED_2.anode
  N21: 2-Channel_Relay.K2-On, LED_2.cathode
  N22: Scope_Frame_Out.OUT, Teensy_3_2.5
  N23: Teensy_3_2.AGND, Teensy_3_2.VUSB
  N24: Teensy_3_2.23, Teensy_3_2.AREF
  N25: Teensy_3_2.22, Teensy_3_2.A10
  N26: Teensy_3_2.21, Teensy_3_2.A11
  N27: Teensy_3_2.13, Teensy_3_2.Program, Teensy_3_2.RST
  N28: Teensy_3_2.8, Scope_Trigger_Out.OUT

custom parts:
  2-Channel 5v Relay Shield: 2 Channel 5v Relay Shield w. 2x SPD-06VDC-SD-C
