# Fritzing sketch pie_scope (saved by Fritzing 0.9.3b)
breadboards: 1

parts:
  Part1 = Adafruit 4-channel I2C-safe Bi-directional Logic Level Converter [part_number="Adafruit #757"]
  Scope_Trigger_In = BNC socket [package=bnc]
  Scope_Trigger_Out = BNC socket [package=bnc]
  Scope_Frame_Out = BNC socket [package=bnc]
  Raspberry_Pi_1 = Raspberry Pi 3 [part_number=RPI-3-V1.2]

nets:
  GND: Part1.GND, Scope_Trigger_In.GND, Scope_Trigger_Out.GND, Scope_Frame_Out.GND, Raspberry_Pi_1.GND
  N1: Part1.A4, Raspberry_Pi_1.GIPO24
  N2: Part1.A2, Raspberry_Pi_1.GIPO23
  N3: Part1.A1, Raspberry_Pi_1.GIPO15
  N4: Part1.LV, Raspberry_Pi_1.3V3
  N5: Part1.B4, Scope_Trigger_Out.OUT
  N6: Part1.B2, Scope_Frame_Out.OUT
  N7: Part1.B1, Scope_Trigger_In.OUT
  N8: Part1.HV, Raspberry_Pi_1.5V

notes:
  3V
  5V
  IR LED (Purple)
  White LED (white)

custom parts:
  Adafruit 4-channel I2C-safe Bi-directional Logic Level Converter: Because the Arduino (and Basic Stamp) are 5V devices, and most modern sensors, displays, flash cards and modes are 3.3V-only, many makers find that they need to perform level shifting/conversion to protect the 3.3V device from 5V. We do have some other handy level shifters in the shop, from the DIP 74LVC245 to the fancy bi-directional TXB0108. However, neither of these are happy to work with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
